# Fritzing sketch station météo (saved by Fritzing 0.9.3b)
breadboards: 1

parts:
  Netduino1 = Netduino Plus2
  LCD1 = LCD screen
  R1 = Trimmer Potentiometer [maximum_resistance=10kΩ package=THT]
  R2 = Resistor [tolerance=±5% resistance=220 package=THT]
  DHT11_1 = DHT22_BLACK_PCB

nets:
  N1: Netduino1.D12_MISO, LCD1.RS
  N2: Netduino1.D11_MOSI, LCD1.E
  N3: Netduino1.D8_CTS1, DHT11_1.connector9
  N4: Netduino1.D5_PWM0, LCD1.DB4
  N5: Netduino1.D4_CS0, LCD1.DB5
  N6: Netduino1.D3_TX1, LCD1.DB6
  N7: Netduino1.D2_RX1, LCD1.DB7
  +5V: Netduino1.+5V, LCD1.VDD, R1.leg1, R2.Pin_0, DHT11_1.connector5
  GND: Netduino1.GND, LCD1.VSS, LCD1.R/W, LCD1.LED-, R1.leg2, DHT11_1.connector6
  N8: LCD1.V0, R1.wiper
  N9: LCD1.LED+, R2.Pin_1
